# Fritzing sketch schematic (saved by Fritzing 0.9.3b)
breadboards: 1

parts:
  Gizwits_WiFi_Witty_ESP-12F1 = Gizwits WiFi Witty ESP-12F
  U1 = 74HC595 SMD [package="SO16 [SMD]"]
  D1 = LTE-302 [package=lte-302]
  VCC1 = 4 x AAA Battery Mount
  D2 = LTE-302 [package=lte-302]
  D3 = LTE-302 [package=lte-302]
  D4 = LTE-302 [package=lte-302]
  D5 = LTE-302 [package=lte-302]
  Part1 = Adafruit Si7021 Temp Humidity [part_number="Adafruit #3251"]

nets:
  N1: Gizwits_WiFi_Witty_ESP-12F1.GPIO14, U1.SH_CP
  N2: Gizwits_WiFi_Witty_ESP-12F1.GPIO13, U1.DS
  VCC: Gizwits_WiFi_Witty_ESP-12F1.VCC, VCC1.+, Part1.VIN
  N3: Gizwits_WiFi_Witty_ESP-12F1.GND, U1.OE, D5.C
  N4: Gizwits_WiFi_Witty_ESP-12F1.GPIO15, U1.ST_CP
  N5: Gizwits_WiFi_Witty_ESP-12F1.GPIO4, Part1.SDA
  N6: Gizwits_WiFi_Witty_ESP-12F1.GPIO5, Part1.SCL
  N7: U1.Q1, D1.A
  N8: U1.Q2, D3.A
  N9: U1.Q3, D2.A
  N10: U1.Q4, D2.C, D4.A
  N11: U1.Q5, D5.A
  GND: U1.GND, D1.C, Part1.GND

custom parts:
  Adafruit Si7021 Temp Humidity: It's summer and you're sweating and your hair's all frizzy and all you really want to know is why the weatherman said this morning that today's relative humidity would max out at a perfectly reasonable 42% when it feels more like 77%. Enter the Si7021 Temperature + Humidity Sensor - the best way to prove the weatherman wrong! This lovely sensor for Silicon labs has ± 3% relative humidity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
